# Fritzing sketch Sensore di distanza per auto (saved by Fritzing 0.8.3b)
circuit board: 16.9333cm x 5.64444cm
breadboards: 1

parts:
  Raspberry_Pi_rev2 = Raspberry Pi rev2
  R5 = Resistor [tolerance=±5% resistance=330 package=THT]
  R6 = Resistor [tolerance=±5% resistance=330 package=THT]
  R7 = Resistor [tolerance=±5% resistance=470 package=THT]
  R8 = Resistor [tolerance=±5% resistance=470 package=THT]
  J2 = Piezo Speaker
  Componente1 = SRF05 Ultrasonic Rangefinder
  Componente2 = SRF05 Ultrasonic Rangefinder
  R9 = Resistor [tolerance=±5% resistance=220 package=THT]
  U1 = LCD-16X2 [package=lcd-16x2]
  R10 = Trimmer Potentiometer [maximum_resistance=10kΩ package=THT]

nets:
  VCC: Raspberry_Pi_rev2.5V, Componente1.VCC, Componente2.VCC
  N1: Raspberry_Pi_rev2.GIPO_2, Componente2.Trig
  N2: Raspberry_Pi_rev2.GIPO_3, R6.Pin_0, R8.Pin_0
  GND: Raspberry_Pi_rev2.GND, R7.Pin_0, R8.Pin_1, Componente1.GND, Componente2.GND, R9.Pin_0
  N3: Raspberry_Pi_rev2.GPIO_17, U1.DB5
  N4: Raspberry_Pi_rev2.GPIO_18, J2.pin2
  N5: Raspberry_Pi_rev2.GPIO_27, U1.DB6
  N6: Raspberry_Pi_rev2.GPIO_22, U1.DB7
  N7: Raspberry_Pi_rev2.GPIO4, Componente1.Trig
  N8: Raspberry_Pi_rev2.GPIO_24, R5.Pin_1, R7.Pin_1
  N9: Raspberry_Pi_rev2.GPIO_25, U1.DB4
  N10: Raspberry_Pi_rev2.GPIO_8, U1.E
  N11: Raspberry_Pi_rev2.GPIO_7, U1.RS
  N12: R5.Pin_0, Componente1.Echo
  N13: R6.Pin_1, Componente2.Echo
  N14: J2.pin1, R9.Pin_1
  N15: U1.VSS, U1.R_W, U1.K, R10.leg2
  N16: U1.VDD, U1.A, R10.leg1
  N17: U1.VO, R10.wiper
